# Fritzing sketch Prophet 12 Button (saved by Fritzing 0.9.3b)
breadboards: 1

parts:
  Part1 = Arduino Nano (Rev3.0)
  R1 = Resistor [tolerance=±5% resistance=220 package=THT]
  LED1 = LED - 5mm [color="Red (633nm)" package="5 mm [THT]"]
  R2 = Resistor [tolerance=±5% resistance=220 package=THT]
  R3 = Resistor [tolerance=±5% resistance=1k package=THT]
  S1 = Momentary Switch [package=ksa_sealed_tac_switch]
  R4 = Resistor [tolerance=±5% resistance=1k package=THT]
  U1 = MIDI_CONN_FEMALE_SUPPORT [package=din_5_female_support]

nets:
  N1: Part1.D1/TX, R2.Pin_0
  N2: Part1.GND, R3.Pin_0, R4.Pin_0, U1.NC1
  N3: Part1.D4, LED1.anode
  N4: Part1.D5, S1.3
  N5: Part1.5V, R1.Pin_0
  N6: R1.Pin_1, U1.MIDI_OUT
  N7: LED1.cathode, R3.Pin_1
  N8: R2.Pin_1, U1.MIDI_IN
  N9: S1.1, R4.Pin_1
